// Logisim project DSDLAB6_Q1.circ as structural Verilog: 1 circuit, main circuit main
module main (
  input  [3:0] B3_B2_B1_B0,
  input  [3:0] A3_A2_A1_A0,
  input  c0,
  output c4,
  output C4_2,
  output [3:0] S3_S2_S1_S0,
  output c3,
  output c2,
  output c1
);

  wire and_1_out, and_2_out, and_3_out, and_4_out, and_5_out, and_6_out, and_7_out, and_8_out, and_9_out,
       and_10_out, and_11_out, and_12_out, and_13_out, and_14_out, xor_1_out, xor_2_out, xor_3_out, xor_4_out;

  xor xor_1 (xor_1_out, B3_B2_B1_B0[3], A3_A2_A1_A0[3]);
  and and_1 (and_1_out, B3_B2_B1_B0[3], A3_A2_A1_A0[3]);
  xor xor_2 (xor_2_out, B3_B2_B1_B0[2], A3_A2_A1_A0[2]);
  and and_2 (and_2_out, B3_B2_B1_B0[2], A3_A2_A1_A0[2]);
  xor xor_3 (xor_3_out, B3_B2_B1_B0[1], A3_A2_A1_A0[1]);
  and and_3 (and_3_out, B3_B2_B1_B0[1], A3_A2_A1_A0[1]);
  xor xor_4 (xor_4_out, B3_B2_B1_B0[0], A3_A2_A1_A0[0]);
  and and_4 (and_4_out, B3_B2_B1_B0[0], A3_A2_A1_A0[0]);
  and and_5 (and_5_out, xor_1_out, xor_2_out, xor_3_out, xor_4_out, c0);
  and and_6 (and_6_out, xor_1_out, xor_2_out, xor_3_out, and_4_out);
  and and_7 (and_7_out, xor_1_out, and_3_out, xor_2_out);
  and and_8 (and_8_out, xor_1_out, xor_4_out);
  and and_9 (and_9_out, c0, xor_2_out, xor_3_out, xor_4_out);
  and and_10 (and_10_out, xor_2_out, xor_3_out, and_4_out);
  and and_11 (and_11_out, xor_2_out, and_3_out);
  and and_12 (and_12_out, xor_3_out, xor_4_out, c0);
  and and_13 (and_13_out, xor_3_out, and_4_out);
  and and_14 (and_14_out, c0, xor_4_out);
  or or_1 (c4, and_5_out, and_6_out, and_7_out, and_8_out, and_1_out);
  or or_2 (c3, and_9_out, and_10_out, and_11_out, and_2_out);
  or or_3 (c2, and_12_out, and_13_out, and_3_out);
  or or_4 (c1, and_14_out, and_4_out);
  xor xor_5 (S3_S2_S1_S0[3], xor_1_out, c3);
  xor xor_6 (S3_S2_S1_S0[2], xor_2_out, c2);
  xor xor_7 (S3_S2_S1_S0[1], xor_3_out, c1);
  xor xor_8 (S3_S2_S1_S0[0], xor_4_out, c0);

  assign C4_2 = c4;

  // Notes on the sheet:
  //   p3
  //   g3
  //   p2
  //   g2
  //   p1
  //   g1
  //   p0
  //   go
  //   p1
  //   p0
  //   p1
  //   p2
  //   p1
  //   g0
  //   c0
  //   p3
  //   p2
  //   p1
  //   c3
  //   c2
  //   c1
  //   p0
  //   c0
endmodule
