// Logisim project DSDLAB7.circ as structural Verilog: 1 circuit, main circuit main
module main (
  input  in_1,
  input  in_2,
  input  in_3,
  input  in_4,
  input  reset,
  input  [3:0] in_6,
  output [3:0] out_7
);

  wire clock_1_out, multiplexer_1_out, multiplexer_2_out, multiplexer_3_out, multiplexer_4_out;

  Clock clock_1 (.out(clock_1_out));
  Multiplexer #(.select(2)) multiplexer_1 (
    .in0(out_7[3]), .in1(in_2), .in2(out_7[2]), .in3(in_6[0]), .out(multiplexer_1_out), .sel({in_4, in_3}));
  D_Flip_Flop d_ff_1 (.D(multiplexer_1_out), .clk(clock_1_out), .Q(out_7[3]), .reset(reset));  // open: Qn, preset
  D_Flip_Flop d_ff_2 (.D(multiplexer_2_out), .clk(clock_1_out), .Q(out_7[2]), .reset(reset));  // open: Qn, preset
  Multiplexer #(.select(2)) multiplexer_2 (
    .in0(out_7[2]), .in1(out_7[3]), .in2(out_7[1]), .in3(in_6[1]), .out(multiplexer_2_out), .sel({in_4, in_3}));
  Multiplexer #(.select(2)) multiplexer_3 (
    .in0(out_7[1]), .in1(out_7[2]), .in2(out_7[0]), .in3(in_6[2]), .out(multiplexer_3_out), .sel({in_4, in_3}));
  D_Flip_Flop d_ff_3 (.D(multiplexer_3_out), .clk(clock_1_out), .Q(out_7[1]), .reset(reset));  // open: Qn, preset
  D_Flip_Flop d_ff_4 (.D(multiplexer_4_out), .clk(clock_1_out), .Q(out_7[0]), .reset(reset));  // open: Qn, preset
  Multiplexer #(.select(2)) multiplexer_4 (
    .in0(out_7[0]), .in1(out_7[1]), .in2(in_1), .in3(in_6[3]), .out(multiplexer_4_out), .sel({in_4, in_3}));

  // Notes on the sheet:
  //   selector lines
  //   10-left shift
  //   01-right shift
  //   input
  //   output
endmodule
